# Fritzing sketch auto-blinds (saved by Fritzing 0.9.3b)
breadboards: 1

parts:
  Part1 = Arduino Nano (Rev3.0)
  DRV_1 = DRV 8825 Stepper Motor Carrier, High Current [part_number="DRV 8825"]  # not connected
  S1 = Toggle Switch [package=THT]
  M1 = Stepper Motor - Bipolar  # not connected
  J4 = Power Jack [package=power_jack_slot]  # not connected
  R2 = Resistor [tolerance=±5% resistance=10k package=THT]

nets:
  N1: Part1.GND, R2.Pin_1
  N2: Part1.D6, Part1.D7, S1.L1, S1.L2, R2.Pin_0
  N3: Part1.3V3, S1.COM
